# Fritzing sketch alimentacionArduino (saved by Fritzing 0.9.3b)

parts:
  Componente1 = Arduino Uno (Rev3)
  VCC1 = 4 x AAA Battery Mount
  S1 = Toggle Switch [package=THT]

nets:
  N1: Componente1.GND, VCC1.-
  N2: Componente1.VIN, S1.COM
