# Fritzing sketch alimentacionDrivers2 (saved by Fritzing 0.9.3b)

parts:
  Driver1 = 28BYJ-48 Driver Module [part_number=ULN2003 package=THT]
  Driver2 = 28BYJ-48 Driver Module [part_number=ULN2003 package=THT]
  VCC1 = 4 x AAA Battery Mount
  S1 = Toggle Switch [package=THT]

nets:
  GND: Driver1.GND, Driver2.GND, VCC1.-
  N1: Driver1.Vmotor, Driver2.Vmotor, S1.L2
  N2: VCC1.+, S1.COM

custom parts:
  28BYJ-48 Driver Module: ULN2003 Driver Module for the 28BYJ-48 Unipolar Stepper Motor LED A - Blue wire - Bottom coil left LED B - Pink wire - Top coil left LED C - Yellow wire - Bottom coil right LED D - Orange wire - Top coil right Common rail - red Connector pins: blue - pink - yellow - orange - red Control pins - IN1 to IN4 Power pins - GND & Vmotor (5-12V) On/Off jumper (if removed, power to motor is cut).
