# Fritzing sketch conexionUS (saved by Fritzing 0.9.3b)

parts:
  hc-sr1 = hc-sr04
  Componente1 = Arduino Uno (Rev3)

nets:
  VCC: hc-sr1.VCC, Componente1.5V
  N1: hc-sr1.Trig, Componente1.D10_PWM/SS
  N2: hc-sr1.Echo, Componente1.D11_PWM/MOSI
  GND: hc-sr1.GND, Componente1.GND

notes:
  Trig -> Pin 10
  Echo -> Pin 11
