# Fritzing sketch sensoresIR (saved by Fritzing 0.9.3b)

parts:
  M1 = fc-51 [package=THT]
  M2 = fc-51 [package=THT]
  Componente1 = Arduino Uno (Rev3)

nets:
  N1: M1.pin1, Componente1.A1
  N2: M1.pin2, M2.pin2, Componente1.GND
  N3: M1.pin3, M2.pin3, Componente1.5V
  N4: M2.pin1, Componente1.A0

notes:
  Sensor izquierdo
  Sensor derecho

custom parts:
  fc-51: Fc-51 Infrared Obstacle Avoidance Proximity Sensor module. IR transmitter led, receiver LED, lm393 compaitor and a pot. 3.3 V to 5V power.
